# Fritzing sketch circuit design (saved by Fritzing 0.9.3b)
breadboards: 1

parts:
  L298N1 = L298N DC motor driver
  M1 = DC Motor
  VCC1 = Battery block 9V
  HC-SR04_Sensor_1 = HC-SR04 Ultrasonic Distance Sensor
  HC-SR04_Sensor_2 = HC-SR04 Ultrasonic Distance Sensor
  HC-SR04_Sensor_3 = HC-SR04 Ultrasonic Distance Sensor
  Raspberry_Pi_1 = Raspberry Pi 3 [part_number=RPI-3-V1.2]
  CUI-enc1 = AMT103
  J1 = Basic Servo
  Part5 = InvenSense MPU6050
  Part6 = Arduino Nano (Rev3.0) (ICSP)

nets:
  N1: L298N1.OUT3, M1.pin_2
  N2: L298N1.OUT4, M1.pin_1
  N3: L298N1.12V, VCC1.+
  N4: L298N1.GND, VCC1.-
  VCC: L298N1.5V#7, HC-SR04_Sensor_1.VCC, HC-SR04_Sensor_2.VCC, HC-SR04_Sensor_3.VCC, CUI-enc1.5V, J1.vcc
  N5: L298N1.5V#10, L298N1.ENB
  N6: L298N1.IN3, Raspberry_Pi_1.GIPO18
  N7: L298N1.IN4, Raspberry_Pi_1.GIPO23
  N8: HC-SR04_Sensor_1.TRIG, Part6.D6
  N9: HC-SR04_Sensor_1.ECHO, Part6.D5
  GND: HC-SR04_Sensor_1.GND, HC-SR04_Sensor_2.GND, HC-SR04_Sensor_3.GND, Raspberry_Pi_1.GND, CUI-enc1.GND, J1.gnd, Part5.GND
  N10: HC-SR04_Sensor_2.TRIG, Part6.D4
  N11: HC-SR04_Sensor_2.ECHO, Part6.D3
  N12: HC-SR04_Sensor_3.TRIG, Part6.D8
  N13: HC-SR04_Sensor_3.ECHO, Part6.D7
  N14: Raspberry_Pi_1.GPIO2, Part5.SDA
  N15: Raspberry_Pi_1.GPIO3, Part5.SCL
  N16: Raspberry_Pi_1.GIPO6, CUI-enc1.A
  N17: Raspberry_Pi_1.GIPO13, J1.pulse
  5V: Raspberry_Pi_1.5V, Part5.VCC

notes:
  Drive Motor
  L298N Motor Driver Board
  9v battery
  rotary encoder
  Mini BreadBoard
  right left and front ultrasonic Sensor
  servo
  mpu9060

custom parts:
  L298N DC motor driver: 2x DC motor driver with 78M05 positive voltage regulator (7..35 V) L298N: max 46 V, 2 A Set 5 V Enable jumper to enable 5 V regultor (needed for the L298N) and +5 V output at screw terminal or supply external +5 V at screw terminal Set ENA and/or ENB to +5 V to enable motor permanently or supply ENA and/or ENB with PWM signal IN1 and IN2 set rotation directory for motor A (OUT1/OUT2) IN2 and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
