# Fritzing sketch wro2024 (saved by Fritzing 1.0.1rc)
breadboards: 1

parts:
  Part1 = Arduino Uno (Rev3)
  Mod1 = Raspberry Pi 4B
  M1 = gear-motor
  IC1 = L293D [package=THT]
  M2 = RioRand LM2596
  M3 = RioRand LM2596
  M4 = RioRand LM2596
  J1 = Basic Servo
  U1 = LIPO-1000mAh [package=lipo-1000]
  MPU9250_MPU-1 = SparkFun IMU Breakout - MPU-9250 [part_number=" SEN-13762"]

nets:
  N1: Part1.D9_PWM, IC1.In_4
  N2: Part1.D10_PWM/SS, J1.pulse
  GND: Part1.GND, Mod1.GND, M3.Pin_4, MPU9250_MPU-1.GND
  N3: Part1.D6_PWM, IC1.In_3
  5V: Part1.5V, Mod1.5V
  N4: Part1.VIN, M3.Pin_3
  3V3: Mod1.3V3, MPU9250_MPU-1.VDD
  N5: Mod1.GPIO2, MPU9250_MPU-1.SDA/SDI
  N6: Mod1.GPIO3, MPU9250_MPU-1.SCL/SCLK
  N7: M1.pin_1, IC1.Out_4_(_Controlled_by_Enable_2_)
  N8: M1.pin_2, IC1.Out_3_(_Controlled_by_Enable_2_)
  N9: IC1.Enable_1, IC1.+V, M4.Pin_3
  N10: IC1.0V, M4.Pin_4
  N11: M2.Pin_1, M3.Pin_1, M4.Pin_1, U1.+
  N12: M2.Pin_2, M3.Pin_2, M4.Pin_2, U1.-
  N13: M2.Pin_3, J1.vcc
  N14: M2.Pin_4, J1.gnd
